# Fritzing sketch bartclock_wiring (saved by Fritzing 0.9.3b)
breadboards: 1

parts:
  C1 = Electrolytic Capacitor [capacitance=1mF package="100 mil [THT, electrolytic]"]
  Power_plug1 = Power plug
  Raspberry_Pi_Zero1 = Raspberry Pi Zero
  Part1 = Logic Level Converter
  LED1 = RGB LED (com. cathode, rbg) [package="5 mm [THT]"]

nets:
  GND: C1.-, Power_plug1.GND, Raspberry_Pi_Zero1.GND, Part1.GND, LED1.red_anode
  N1: C1.+, Power_plug1.VCC, LED1.green_anode
  N2: Raspberry_Pi_Zero1.3v3, Part1.LV
  N3: Raspberry_Pi_Zero1.GPIO24, Part1.TX_LV
  N4: Raspberry_Pi_Zero1.GPIO23, Part1.TX2_LV
  N5: Part1.TX_HV, LED1.common_cathode
  N6: Part1.TX2_HV, LED1.blue_anode
